// Logisim project Projeto1.circ as structural Verilog: 1 circuit, main circuit main
module main (
  input  in_1,
  input  in_2,
  input  in_3,
  input  in_4,
  input  in_5,
  input  in_6,
  input  in_7,
  input  in_8,
  input  [1:0] in_9,
  output out_10,
  output out_11,
  output out_12,
  output out_13
);

  wire clock_1_out, clock_2_out, multiplexer_1_out, multiplexer_2_out, multiplexer_3_out, multiplexer_4_out,
       multiplexer_5_out, undriven;
  wire [3:0] adder_1_out, d_ff_5_q;
  wire [3:1] undriven_2;

  Multiplexer #(.select(2)) multiplexer_1 (
    .in0(out_10), .in1(in_1), .in2(out_11), .in3(in_3), .out(multiplexer_1_out), .sel(in_9));  // open: en
  Multiplexer #(.select(2)) multiplexer_2 (
    .in0(out_11), .in1(out_10), .in2(out_12), .in3(in_5), .out(multiplexer_2_out), .sel(in_9));  // open: en
  Multiplexer #(.select(2)) multiplexer_3 (
    .in0(out_12), .in1(out_11), .in2(out_13), .in3(in_6), .out(multiplexer_3_out), .sel(in_9));  // open: en
  Multiplexer #(.select(2)) multiplexer_4 (
    .in0(out_13), .in1(out_12), .in2(in_7), .in3(in_8), .out(multiplexer_4_out), .sel(in_9));  // open: en
  Clock clock_1 (.out(clock_1_out));
  D_Flip_Flop d_ff_1 (.clk(clock_1_out), .D(multiplexer_1_out), .Q(out_10), .en(undriven));  // open: Qn, preset, reset
  D_Flip_Flop d_ff_2 (.clk(clock_1_out), .D(multiplexer_2_out), .Q(out_11));  // open: Qn, preset, en, reset
  D_Flip_Flop d_ff_3 (.clk(clock_1_out), .D(multiplexer_3_out), .Q(out_12));  // open: Qn, preset, en, reset
  D_Flip_Flop d_ff_4 (.clk(clock_1_out), .D(multiplexer_4_out), .Q(out_13));  // open: Qn, preset, en, reset
  Adder #(.width(4)) adder_1 (.a(d_ff_5_q), .b({undriven_2, in_2}), .out(adder_1_out));  // open: cin, cout
  Multiplexer multiplexer_5 (.in0(d_ff_5_q[0]), .in1(adder_1_out[0]), .out(multiplexer_5_out), .sel(in_4));  // open: en
  Clock clock_2 (.out(clock_2_out));
  D_Flip_Flop d_ff_5 (.clk(clock_2_out), .D(multiplexer_5_out), .Q(d_ff_5_q[0]));  // open: Qn, preset, en, reset
  // Pins of 1 and 4 bits meet at {undriven_2, in_2}
  // Pins of 1 and 4 bits meet at d_ff_5_q
  // Pins of 1 and 4 bits meet at adder_1_out
endmodule
