// Logisim project Registrador de 4 mux.circ as structural Verilog: 1 circuit, main circuit main
module main (
  input  in_1,
  input  in_2,
  input  in_3,
  input  in_4,
  input  in_5,
  output out_6,
  output out_7,
  output out_8,
  output out_9
);

  wire clock_1_out, multiplexer_1_out, multiplexer_2_out, multiplexer_3_out, multiplexer_4_out;

  Multiplexer multiplexer_1 (.in0(out_6), .in1(in_1), .out(multiplexer_1_out), .sel(in_5));  // open: en
  Multiplexer multiplexer_2 (.in0(out_7), .in1(in_2), .out(multiplexer_2_out), .sel(in_5));  // open: en
  Multiplexer multiplexer_3 (.in0(out_8), .in1(in_3), .out(multiplexer_3_out), .sel(in_5));  // open: en
  Multiplexer multiplexer_4 (.in0(out_9), .in1(in_4), .out(multiplexer_4_out), .sel(in_5));  // open: en
  Clock clock_1 (.out(clock_1_out));
  D_Flip_Flop d_ff_1 (.clk(clock_1_out), .D(multiplexer_1_out), .Q(out_6));  // open: Qn, preset, en, reset
  D_Flip_Flop d_ff_2 (.clk(clock_1_out), .D(multiplexer_2_out), .Q(out_7));  // open: Qn, preset, en, reset
  D_Flip_Flop d_ff_3 (.clk(clock_1_out), .D(multiplexer_3_out), .Q(out_8));  // open: Qn, preset, en, reset
  D_Flip_Flop d_ff_4 (.clk(clock_1_out), .D(multiplexer_4_out), .Q(out_9));  // open: Qn, preset, en, reset
endmodule
